# Fritzing sketch Router Restarter Schematic (saved by Fritzing 0.9.2b)
perfboards: 1

parts:
  Power_plug1 = Power plug
  Power_plug2 = Power plug
  Q1 = NPN-Transistor [part_number=2N4401 package="TO92 [THT]"]
  DIP-Relay1 = DIP-Relay-D31A [part_number=D31A*]
  R1 = Resistor [tolerance=±5% resistance=220 package=THT]
  J1 = female pin header, 2 pins [form="♀ (female)"]

nets:
  GND: Power_plug1.GND, Power_plug2.GND, Q1.E, J1.pin1
  N1: Power_plug1.VCC, DIP-Relay1.A1_Switch_Terminal_A, DIP-Relay1.COIL1_+
  N2: Power_plug2.VCC, DIP-Relay1.B2_Switch_Terminal_B
  N3: Q1.B, R1.Pin_1
  N4: Q1.C, DIP-Relay1.Coil2_-
  N5: R1.Pin_0, J1.pin2

notes:
  12v from receptacle
  12v to Router
  Control from RasPi
  Logic signal (5v)
  Common
  Router Restarter, Interface to allow Raspberry Pi to restart router when internet connection is lost., 1
